// Logisim project Game.circ as structural Verilog
module main (
  input  in_1
);

  wire ResetBar_out;
  wire [31:0] barhandler_1_output;

  Button L (.out(in_1));
  BarHandler barhandler_1 (.reset(ResetBar_out), .R(in_1), .L(in_1), .\output (barhandler_1_output));
  Button ResetBar (.out(ResetBar_out));
  DotMatrix #(.inputtype("row"), .matrixcols(32), .matrixrows(32), .dotshape("circle")) dotmatrix_1 (.row31(barhandler_1_output));  // open: row0, row1, row2, row3, row4, row5, row6, row7, row8, row9, row10, row11, row12, row13, row14, row15, row16, row17, row18, row19, row20, row21, row22, row23, row24, row25, row26, row27, row28, row29, row30
  // Probe on barhandler_1_output
endmodule

module BarHandler (
  input  reset,
  input  R,
  input  L,
  output [31:0] \output 
);

  wire clock, L_t, Left, R_t, Reset_t, reset_t_t, Right, update;
  wire [31:0] divider_1_out, multiplexer_1_out, multiplier_1_out, register_1_q;

  Clock clock_1 (.out(clock));
  or or_1 (R_t, R, Right);
  or or_2 (L_t, L, Left);
  or or_3 (reset_t_t, reset, Reset_t);
  or or_4 (update, R_t, L_t, reset_t_t);
  Multiplexer #(.width(32)) multiplexer_1 (
    .in0(\output ), .in1(32'h3c000), .out(multiplexer_1_out), .sel(reset_t_t));  // open: en
  Register #(.width(32)) register_1 (.D(multiplexer_1_out), .en(update), .Q(register_1_q), .clk(clock));  // open: clr
  DotMatrix #(.inputtype("row"), .matrixcols(32), .matrixrows(2)) dotmatrix_1 (.row1(\output ));  // open: row0
  // Probe on register_1_q
  Button button_1 (.out(Right));
  Multiplier #(.width(32)) multiplier_1 (.a(register_1_q), .b(32'h2), .out(multiplier_1_out));  // open: cin, cout
  Divider #(.width(32)) divider_1 (.a(register_1_q), .b(32'h2), .out(divider_1_out));  // open: upper, rem
  Button button_2 (.out(Reset_t));
  Button button_3 (.out(Left));
  Multiplexer #(.width(32)) multiplexer_2 (
    .in0(multiplier_1_out), .in1(divider_1_out), .out(\output ), .sel(R_t));  // open: en

  // Other names for the same wires on the sheet: out[31:0] = \output 
endmodule
